// Logisim project Rtype.circ as structural Verilog: 4 circuits, main circuit main
module main (
  input  in_1,
  input  in_2,
  output [31:0] out_3,
  output [31:0] out_4,
  output [4:0] _10,
  output [4:0] _18,
  output [4:0] _17,
  output [7:0] out_8,
  output [7:0] out_9,
  output [7:0] out_10,
  output [7:0] out_11,
  output [1:0] _2,
  output [31:0] out_13,
  output out_14
);

  wire clock_1_out;
  wire [7:0] adder_1_out, bit_extender_1_out, register_1_q;

  assign bit_extender_1_out = {{7{1'b0}}, 1'b1};  // Bit_Extender bit_extender_1
  Clock clock_1 (.out(clock_1_out));
  Adder adder_1 (.a(bit_extender_1_out), .b(register_1_q), .out(adder_1_out));  // open: cin, cout
  Register register_1 (.D(adder_1_out), .Q(register_1_q), .clk(clock_1_out));  // open: en, clr
  ROM #(.dataWidth(32)) rom_1 (.addr(register_1_q), .data({out_8, out_9, out_10, out_11}));  // open: sel
  Bit_Extender #(.out_width(5)) bit_extender_2 (.in(out_11), .out(_10));
  Bit_Extender #(.out_width(5)) bit_extender_3 (.in(out_10), .out(_18));
  Bit_Extender #(.out_width(5)) bit_extender_4 (.in(out_9), .out(_17));
  Bit_Extender #(.out_width(2)) bit_extender_5 (.in(out_8), .out(_2));
  _32bitreg ID (
    .clock(clock_1_out), .Write_Data(out_13), .WriteRegister(_10), .ReadReg_1_RS(_18), .ReadReg_2_RT(_17),
    .ReadData_1(out_3), .RegWrite(in_2), .ReadData_2(out_4));
  _32bit_ALU u_32bit_alu_1 (
    .ALUop(_2), .B(out_4), .A(out_3), .cout(out_14), .Result(out_13), .Cin(in_1));  // open: Overflow, zero

  // Notes on the sheet:
  //   contents of rom_1 (hex, n*v repeats v):
  //   211120a
endmodule

module _1_Bit_ALU (
  input  Cin,
  input  A,
  input  B,
  input  [1:0] ALUop,
  output out_5,
  output out_6
);

  wire adder_1_out, and_1_out, and_2_out, multiplexer_1_out, not_1_out, or_1_out;

  not not_1 (not_1_out, B);
  and and_1 (and_1_out, B, A);
  or or_1 (or_1_out, B, A);
  Multiplexer #(.enable("false")) multiplexer_1 (.in0(B), .in1(not_1_out), .out(multiplexer_1_out), .sel(and_2_out));
  and and_2 (and_2_out, ALUop[1], ALUop[0]);
  Multiplexer #(.select(2), .enable("false")) multiplexer_2 (
    .in0(and_1_out), .in1(or_1_out), .in2(adder_1_out), .in3(adder_1_out), .out(out_5), .sel(ALUop));
  Adder #(.width(1)) adder_1 (.a(A), .b(multiplexer_1_out), .out(adder_1_out), .cin(Cin), .cout(out_6));
endmodule

module _32bit_ALU (
  input  Cin,
  input  [1:0] ALUop,
  input  [31:0] A,
  input  [31:0] B,
  output cout,
  output Overflow,
  output [31:0] Result,
  output zero
);

  wire and_2_out, multiplexer_1_out, n1_bit_alu_1_out_6, n1_bit_alu_2_out_6, n1_bit_alu_3_out_6,
       n1_bit_alu_4_out_6, n1_bit_alu_5_out_6, n1_bit_alu_6_out_6, n1_bit_alu_7_out_6, n1_bit_alu_8_out_6,
       n1_bit_alu_9_out_6, n1_bit_alu_10_out_6, n1_bit_alu_11_out_6, n1_bit_alu_12_out_6,
       n1_bit_alu_13_out_6, n1_bit_alu_14_out_6, n1_bit_alu_15_out_6, n1_bit_alu_16_out_6,
       n1_bit_alu_17_out_6, n1_bit_alu_18_out_6, n1_bit_alu_19_out_6, n1_bit_alu_20_out_6,
       n1_bit_alu_21_out_6, n1_bit_alu_22_out_6, n1_bit_alu_23_out_6, n1_bit_alu_24_out_6,
       n1_bit_alu_25_out_6, n1_bit_alu_26_out_6, n1_bit_alu_27_out_6, n1_bit_alu_28_out_6,
       n1_bit_alu_29_out_6, n1_bit_alu_30_out_6, n1_bit_alu_31_out_6;

  and and_1 (Overflow, B[31], A[31]);
  and and_2 (and_2_out, ALUop[1], ALUop[0]);
  _1_Bit_ALU u_1_bit_alu_1 (
    .out_5(Result[0]), .out_6(n1_bit_alu_1_out_6), .Cin(multiplexer_1_out), .A(A[0]), .B(B[0]), .ALUop(ALUop));
  _1_Bit_ALU u_1_bit_alu_2 (
    .out_5(Result[1]), .out_6(n1_bit_alu_2_out_6), .Cin(n1_bit_alu_1_out_6), .A(A[1]), .B(B[1]), .ALUop(ALUop));
  _1_Bit_ALU u_1_bit_alu_3 (
    .out_5(Result[2]), .out_6(n1_bit_alu_3_out_6), .Cin(n1_bit_alu_2_out_6), .A(A[2]), .B(B[2]), .ALUop(ALUop));
  _1_Bit_ALU u_1_bit_alu_4 (
    .out_5(Result[3]), .out_6(n1_bit_alu_4_out_6), .Cin(n1_bit_alu_3_out_6), .A(A[3]), .B(B[3]), .ALUop(ALUop));
  _1_Bit_ALU u_1_bit_alu_5 (
    .out_5(Result[4]), .out_6(n1_bit_alu_5_out_6), .Cin(n1_bit_alu_4_out_6), .A(A[4]), .B(B[4]), .ALUop(ALUop));
  _1_Bit_ALU u_1_bit_alu_6 (
    .out_5(Result[5]), .out_6(n1_bit_alu_6_out_6), .Cin(n1_bit_alu_5_out_6), .A(A[5]), .B(B[5]), .ALUop(ALUop));
  _1_Bit_ALU u_1_bit_alu_7 (
    .out_5(Result[6]), .out_6(n1_bit_alu_7_out_6), .Cin(n1_bit_alu_6_out_6), .A(A[6]), .B(B[6]), .ALUop(ALUop));
  _1_Bit_ALU u_1_bit_alu_8 (
    .out_5(Result[7]), .out_6(n1_bit_alu_8_out_6), .Cin(n1_bit_alu_7_out_6), .A(A[7]), .B(B[7]), .ALUop(ALUop));
  _1_Bit_ALU u_1_bit_alu_9 (
    .out_5(Result[8]), .out_6(n1_bit_alu_9_out_6), .Cin(n1_bit_alu_8_out_6), .A(A[8]), .B(B[8]), .ALUop(ALUop));
  _1_Bit_ALU u_1_bit_alu_10 (
    .out_5(Result[9]), .out_6(n1_bit_alu_10_out_6), .Cin(n1_bit_alu_9_out_6), .A(A[9]), .B(B[9]),
    .ALUop(ALUop));
  _1_Bit_ALU u_1_bit_alu_11 (
    .out_5(Result[10]), .out_6(n1_bit_alu_11_out_6), .Cin(n1_bit_alu_10_out_6), .A(A[10]), .B(B[10]),
    .ALUop(ALUop));
  _1_Bit_ALU u_1_bit_alu_12 (
    .out_5(Result[11]), .out_6(n1_bit_alu_12_out_6), .Cin(n1_bit_alu_11_out_6), .A(A[11]), .B(B[11]),
    .ALUop(ALUop));
  _1_Bit_ALU u_1_bit_alu_13 (
    .out_5(Result[12]), .out_6(n1_bit_alu_13_out_6), .Cin(n1_bit_alu_12_out_6), .A(A[12]), .B(B[12]),
    .ALUop(ALUop));
  _1_Bit_ALU u_1_bit_alu_14 (
    .out_5(Result[13]), .out_6(n1_bit_alu_14_out_6), .Cin(n1_bit_alu_13_out_6), .A(A[13]), .B(B[13]),
    .ALUop(ALUop));
  _1_Bit_ALU u_1_bit_alu_15 (
    .out_5(Result[14]), .out_6(n1_bit_alu_15_out_6), .Cin(n1_bit_alu_14_out_6), .A(A[14]), .B(B[14]),
    .ALUop(ALUop));
  _1_Bit_ALU u_1_bit_alu_16 (
    .out_5(Result[15]), .out_6(n1_bit_alu_16_out_6), .Cin(n1_bit_alu_15_out_6), .A(A[15]), .B(B[15]),
    .ALUop(ALUop));
  _1_Bit_ALU u_1_bit_alu_17 (
    .out_5(Result[16]), .out_6(n1_bit_alu_17_out_6), .Cin(n1_bit_alu_16_out_6), .A(A[16]), .B(B[16]),
    .ALUop(ALUop));
  _1_Bit_ALU u_1_bit_alu_18 (
    .out_5(Result[17]), .out_6(n1_bit_alu_18_out_6), .Cin(n1_bit_alu_17_out_6), .A(A[17]), .B(B[17]),
    .ALUop(ALUop));
  _1_Bit_ALU u_1_bit_alu_19 (
    .out_5(Result[18]), .out_6(n1_bit_alu_19_out_6), .Cin(n1_bit_alu_18_out_6), .A(A[18]), .B(B[18]),
    .ALUop(ALUop));
  _1_Bit_ALU u_1_bit_alu_20 (
    .out_5(Result[19]), .out_6(n1_bit_alu_20_out_6), .Cin(n1_bit_alu_19_out_6), .A(A[19]), .B(B[19]),
    .ALUop(ALUop));
  _1_Bit_ALU u_1_bit_alu_21 (
    .out_5(Result[20]), .out_6(n1_bit_alu_21_out_6), .Cin(n1_bit_alu_20_out_6), .A(A[20]), .B(B[20]),
    .ALUop(ALUop));
  _1_Bit_ALU u_1_bit_alu_22 (
    .out_5(Result[21]), .out_6(n1_bit_alu_22_out_6), .Cin(n1_bit_alu_21_out_6), .A(A[21]), .B(B[21]),
    .ALUop(ALUop));
  _1_Bit_ALU u_1_bit_alu_23 (
    .out_5(Result[22]), .out_6(n1_bit_alu_23_out_6), .Cin(n1_bit_alu_22_out_6), .A(A[22]), .B(B[22]),
    .ALUop(ALUop));
  _1_Bit_ALU u_1_bit_alu_24 (
    .out_5(Result[23]), .out_6(n1_bit_alu_24_out_6), .Cin(n1_bit_alu_23_out_6), .A(A[23]), .B(B[23]),
    .ALUop(ALUop));
  _1_Bit_ALU u_1_bit_alu_25 (
    .out_5(Result[24]), .out_6(n1_bit_alu_25_out_6), .Cin(n1_bit_alu_24_out_6), .A(A[24]), .B(B[24]),
    .ALUop(ALUop));
  _1_Bit_ALU u_1_bit_alu_26 (
    .out_5(Result[25]), .out_6(n1_bit_alu_26_out_6), .Cin(n1_bit_alu_25_out_6), .A(A[25]), .B(B[25]),
    .ALUop(ALUop));
  _1_Bit_ALU u_1_bit_alu_27 (
    .out_5(Result[26]), .out_6(n1_bit_alu_27_out_6), .Cin(n1_bit_alu_26_out_6), .A(A[26]), .B(B[26]),
    .ALUop(ALUop));
  _1_Bit_ALU u_1_bit_alu_28 (
    .out_5(Result[27]), .out_6(n1_bit_alu_28_out_6), .Cin(n1_bit_alu_27_out_6), .A(A[27]), .B(B[27]),
    .ALUop(ALUop));
  _1_Bit_ALU u_1_bit_alu_29 (
    .out_5(Result[28]), .out_6(n1_bit_alu_29_out_6), .Cin(n1_bit_alu_28_out_6), .A(A[28]), .B(B[28]),
    .ALUop(ALUop));
  _1_Bit_ALU u_1_bit_alu_30 (
    .out_5(Result[29]), .out_6(n1_bit_alu_30_out_6), .Cin(n1_bit_alu_29_out_6), .A(A[29]), .B(B[29]),
    .ALUop(ALUop));
  _1_Bit_ALU u_1_bit_alu_31 (
    .out_5(Result[30]), .out_6(n1_bit_alu_31_out_6), .Cin(n1_bit_alu_30_out_6), .A(A[30]), .B(B[30]),
    .ALUop(ALUop));
  _1_Bit_ALU u_1_bit_alu_32 (
    .out_5(Result[31]), .out_6(cout), .Cin(n1_bit_alu_31_out_6), .A(A[31]), .B(B[31]), .ALUop(ALUop));
  Multiplexer #(.enable("false")) multiplexer_1 (.in0(Cin), .in1(1'b1), .out(multiplexer_1_out), .sel(and_2_out));
  nor nor_1 (zero, Result[0], Result[1], Result[2], Result[3], Result[4], Result[5], Result[6], Result[7], Result[8], Result[9], Result[10], Result[11], Result[12], Result[13], Result[14], Result[15], Result[16], Result[17], Result[18], Result[19], Result[20], Result[21], Result[22], Result[23], Result[24], Result[25], Result[26], Result[27], Result[28], Result[29], Result[30], Result[31]);
endmodule

module _32bitreg (
  input  clock,
  input  [31:0] Write_Data,
  input  RegWrite,
  input  [4:0] ReadReg_1_RS,
  input  [4:0] ReadReg_2_RT,
  input  [4:0] WriteRegister,
  output [31:0] ReadData_1,
  output [31:0] ReadData_2
);

  wire and_1_out, and_2_out, and_3_out, and_4_out, and_5_out, and_6_out, and_7_out, and_8_out, and_9_out,
       and_10_out, and_11_out, and_12_out, and_13_out, and_14_out, and_15_out, and_16_out, and_17_out,
       and_18_out, and_19_out, and_20_out, and_21_out, and_22_out, and_23_out, and_24_out, and_25_out,
       and_26_out, and_27_out, and_28_out, and_29_out, and_30_out, and_31_out, and_32_out, decoder_1_out0,
       decoder_1_out1, decoder_1_out2, decoder_1_out3, decoder_1_out4, decoder_1_out5, decoder_1_out6,
       decoder_1_out7, decoder_1_out8, decoder_1_out9, decoder_1_out10, decoder_1_out11, decoder_1_out12,
       decoder_1_out13, decoder_1_out14, decoder_1_out15, decoder_1_out16, decoder_1_out17, decoder_1_out18,
       decoder_1_out19, decoder_1_out20, decoder_1_out21, decoder_1_out22, decoder_1_out23, decoder_1_out24,
       decoder_1_out25, decoder_1_out26, decoder_1_out27, decoder_1_out28, decoder_1_out29, decoder_1_out30,
       decoder_1_out31;
  wire [31:0] s16_q, s17_q, s18_q, t0_2_q, t0_q, t1_2_q, t1_q, t2_q, t3_q, t4_q, t5_q, t6_q, t7_q, t10_q,
       t11_q, t12_q, t13_q, t14_q, t15_q, t19_q, t20_q, t21_q, t22_q, t23_q, t24_q, t25_q, t26_q, t27_q,
       t28_q, t29_q, t30_q, t31_q;

  Decoder #(.select(5), .enable("false")) decoder_1 (
    .out0(decoder_1_out0), .out1(decoder_1_out1), .out2(decoder_1_out2), .out3(decoder_1_out3),
    .out4(decoder_1_out4), .out5(decoder_1_out5), .out6(decoder_1_out6), .out7(decoder_1_out7),
    .out8(decoder_1_out8), .out9(decoder_1_out9), .out10(decoder_1_out10), .out11(decoder_1_out11),
    .out12(decoder_1_out12), .out13(decoder_1_out13), .out14(decoder_1_out14), .out15(decoder_1_out15),
    .out16(decoder_1_out16), .out17(decoder_1_out17), .out18(decoder_1_out18), .out19(decoder_1_out19),
    .out20(decoder_1_out20), .out21(decoder_1_out21), .out22(decoder_1_out22), .out23(decoder_1_out23),
    .out24(decoder_1_out24), .out25(decoder_1_out25), .out26(decoder_1_out26), .out27(decoder_1_out27),
    .out28(decoder_1_out28), .out29(decoder_1_out29), .out30(decoder_1_out30), .out31(decoder_1_out31),
    .sel(WriteRegister));
  and and_1 (and_1_out, decoder_1_out0, RegWrite);
  and and_2 (and_2_out, decoder_1_out1, RegWrite);
  and and_3 (and_3_out, decoder_1_out2, RegWrite);
  and and_4 (and_4_out, decoder_1_out3, RegWrite);
  and and_5 (and_5_out, decoder_1_out4, RegWrite);
  and and_6 (and_6_out, decoder_1_out5, RegWrite);
  and and_7 (and_7_out, decoder_1_out6, RegWrite);
  and and_8 (and_8_out, decoder_1_out7, RegWrite);
  and and_9 (and_9_out, decoder_1_out8, RegWrite);
  and and_10 (and_10_out, decoder_1_out9, RegWrite);
  and and_11 (and_11_out, decoder_1_out10, RegWrite);
  and and_12 (and_12_out, decoder_1_out11, RegWrite);
  and and_13 (and_13_out, decoder_1_out12, RegWrite);
  and and_14 (and_14_out, decoder_1_out13, RegWrite);
  and and_15 (and_15_out, decoder_1_out14, RegWrite);
  and and_16 (and_16_out, decoder_1_out15, RegWrite);
  and and_17 (and_17_out, decoder_1_out16, RegWrite);
  and and_18 (and_18_out, decoder_1_out17, RegWrite);
  and and_19 (and_19_out, decoder_1_out18, RegWrite);
  and and_20 (and_20_out, decoder_1_out19, RegWrite);
  and and_21 (and_21_out, decoder_1_out20, RegWrite);
  and and_22 (and_22_out, decoder_1_out21, RegWrite);
  and and_23 (and_23_out, decoder_1_out22, RegWrite);
  and and_24 (and_24_out, decoder_1_out23, RegWrite);
  and and_25 (and_25_out, decoder_1_out24, RegWrite);
  and and_26 (and_26_out, decoder_1_out25, RegWrite);
  and and_27 (and_27_out, decoder_1_out26, RegWrite);
  and and_28 (and_28_out, decoder_1_out27, RegWrite);
  and and_29 (and_29_out, decoder_1_out28, RegWrite);
  and and_30 (and_30_out, decoder_1_out29, RegWrite);
  and and_31 (and_31_out, decoder_1_out30, RegWrite);
  and and_32 (and_32_out, decoder_1_out31, RegWrite);
  Register #(.width(32)) t0 (.D(Write_Data), .en(and_1_out), .Q(t0_q), .clk(clock));  // open: clr
  Register #(.width(32)) t1 (.D(Write_Data), .en(and_2_out), .Q(t1_q), .clk(clock));  // open: clr
  Register #(.width(32)) t2 (.D(Write_Data), .en(and_3_out), .Q(t2_q), .clk(clock));  // open: clr
  Register #(.width(32)) t3 (.D(Write_Data), .en(and_4_out), .Q(t3_q), .clk(clock));  // open: clr
  Register #(.width(32)) t4 (.D(Write_Data), .en(and_5_out), .Q(t4_q), .clk(clock));  // open: clr
  Register #(.width(32)) t5 (.D(Write_Data), .en(and_6_out), .Q(t5_q), .clk(clock));  // open: clr
  Register #(.width(32)) t6 (.D(Write_Data), .en(and_7_out), .Q(t6_q), .clk(clock));  // open: clr
  Register #(.width(32)) t7 (.D(Write_Data), .en(and_8_out), .Q(t7_q), .clk(clock));  // open: clr
  Register #(.width(32)) t0_2 (.D(Write_Data), .en(and_9_out), .Q(t0_2_q), .clk(clock));  // open: clr
  Register #(.width(32)) t1_2 (.D(Write_Data), .en(and_10_out), .Q(t1_2_q), .clk(clock));  // open: clr
  Register #(.width(32)) t10 (.D(Write_Data), .en(and_11_out), .Q(t10_q), .clk(clock));  // open: clr
  Register #(.width(32)) t11 (.D(Write_Data), .en(and_12_out), .Q(t11_q), .clk(clock));  // open: clr
  Register #(.width(32)) t12 (.D(Write_Data), .en(and_13_out), .Q(t12_q), .clk(clock));  // open: clr
  Register #(.width(32)) t13 (.D(Write_Data), .en(and_14_out), .Q(t13_q), .clk(clock));  // open: clr
  Register #(.width(32)) t14 (.D(Write_Data), .en(and_15_out), .Q(t14_q), .clk(clock));  // open: clr
  Register #(.width(32)) t15 (.D(Write_Data), .en(and_16_out), .Q(t15_q), .clk(clock));  // open: clr
  Register #(.width(32)) s16 (.D(Write_Data), .en(and_17_out), .Q(s16_q), .clk(clock));  // open: clr
  Register #(.width(32)) s17 (.D(Write_Data), .en(and_18_out), .Q(s17_q), .clk(clock));  // open: clr
  Register #(.width(32)) s18 (.D(Write_Data), .en(and_19_out), .Q(s18_q), .clk(clock));  // open: clr
  Register #(.width(32)) t19 (.D(Write_Data), .en(and_20_out), .Q(t19_q), .clk(clock));  // open: clr
  Register #(.width(32)) t20 (.D(Write_Data), .en(and_21_out), .Q(t20_q), .clk(clock));  // open: clr
  Register #(.width(32)) t21 (.D(Write_Data), .en(and_22_out), .Q(t21_q), .clk(clock));  // open: clr
  Register #(.width(32)) t22 (.D(Write_Data), .en(and_23_out), .Q(t22_q), .clk(clock));  // open: clr
  Register #(.width(32)) t23 (.D(Write_Data), .en(and_24_out), .Q(t23_q), .clk(clock));  // open: clr
  Register #(.width(32)) t24 (.D(Write_Data), .en(and_25_out), .Q(t24_q), .clk(clock));  // open: clr
  Register #(.width(32)) t25 (.D(Write_Data), .en(and_26_out), .Q(t25_q), .clk(clock));  // open: clr
  Register #(.width(32)) t26 (.D(Write_Data), .en(and_27_out), .Q(t26_q), .clk(clock));  // open: clr
  Register #(.width(32)) t27 (.D(Write_Data), .en(and_28_out), .Q(t27_q), .clk(clock));  // open: clr
  Register #(.width(32)) t28 (.D(Write_Data), .en(and_29_out), .Q(t28_q), .clk(clock));  // open: clr
  Register #(.width(32)) t29 (.D(Write_Data), .en(and_30_out), .Q(t29_q), .clk(clock));  // open: clr
  Register #(.width(32)) t30 (.D(Write_Data), .en(and_31_out), .Q(t30_q), .clk(clock));  // open: clr
  Register #(.width(32)) t31 (.D(Write_Data), .en(and_32_out), .Q(t31_q), .clk(clock));  // open: clr
  Multiplexer #(.select(5), .width(32), .enable("false")) multiplexer_1 (
    .in0(t0_q), .in1(t1_q), .in2(t2_q), .in3(t3_q), .in4(t4_q), .in5(t5_q), .in6(t6_q), .in7(t7_q),
    .in8(t0_2_q), .in9(t1_2_q), .in10(t10_q), .in11(t11_q), .in12(t12_q), .in13(t13_q), .in14(t14_q),
    .in15(t15_q), .in16(s16_q), .in17(s17_q), .in18(s18_q), .in19(t19_q), .in20(t20_q), .in21(t21_q),
    .in22(t22_q), .in23(t23_q), .in24(t24_q), .in25(t25_q), .in26(t26_q), .in27(t27_q), .in28(t28_q),
    .in29(t29_q), .in30(t30_q), .in31(t31_q), .out(ReadData_1), .sel(ReadReg_1_RS));
  Multiplexer #(.select(5), .width(32), .enable("false")) multiplexer_2 (
    .in0(t0_q), .in1(t1_q), .in2(t2_q), .in3(t3_q), .in4(t4_q), .in5(t5_q), .in6(t6_q), .in7(t7_q),
    .in8(t0_2_q), .in9(t1_2_q), .in10(t10_q), .in11(t11_q), .in12(t12_q), .in13(t13_q), .in14(t14_q),
    .in15(t15_q), .in16(s16_q), .in17(s17_q), .in18(s18_q), .in19(t19_q), .in20(t20_q), .in21(t21_q),
    .in22(t22_q), .in23(t23_q), .in24(t24_q), .in25(t25_q), .in26(t26_q), .in27(t27_q), .in28(t28_q),
    .in29(t29_q), .in30(t30_q), .in31(t31_q), .out(ReadData_2), .sel(ReadReg_2_RT));
endmodule
